// Logisim project Project1.circ as structural Verilog: 11 circuits, main circuit main
module main (
  input  [3:0] A,
  input  [3:0] B,
  input  [1:0] Base_Selector,
  input  Operation
);

  wire LSB_0_1, LSB_0_2, LSB_0_3, LSB_0_4, LSB_0_5, LSB_0_67, LSB_1_1, LSB_1_2, LSB_1_3, LSB_1_4, LSB_1_5,
       LSB_1_67, LSB_2_1, LSB_2_2, LSB_2_3, LSB_2_4, LSB_2_5, LSB_2_67, LSB_3_1, LSB_3_2, LSB_3_3, LSB_3_4,
       LSB_3_5, LSB_3_67, LSB_4_1, LSB_4_2, LSB_4_3, LSB_4_4, LSB_4_5, LSB_4_67, LSB_5_1, LSB_5_2, LSB_5_3,
       LSB_5_4, LSB_5_5, LSB_5_67, LSB_6_1, LSB_6_2, LSB_6_3, LSB_6_4, LSB_6_5, LSB_6_67;
  wire [4:0] operation_1_out_4;
  wire [6:0] base9_out_2, base9_out_3, octal_out_2, octal_out_3;

  Hex_Digit_Display hex_digit_display_1 (.value(A));  // open: dp
  Hex_Digit_Display hex_digit_display_2 (.value(B));  // open: dp
  Operation operation_1 (.Input_1(A), .Input_2(B), .Operation(Operation), .out_4(operation_1_out_4));
  _7_Segment_Display u_7_segment_display_1 (
    .g(LSB_6_67), .f(LSB_5_67), .a(LSB_0_67), .b(LSB_1_67), .e(LSB_4_67), .d(LSB_3_67), .c(LSB_2_67));  // open: dp
  convert_to_octal__all octal (.in_1(operation_1_out_4), .out_2(octal_out_2), .out_3(octal_out_3));
  convert_to_base9__all base9 (.in_1(operation_1_out_4), .out_2(base9_out_2), .out_3(base9_out_3));
  _7_Segment_Display u_7_segment_display_2 (
    .g(LSB_6_67), .f(LSB_5_67), .a(LSB_0_67), .b(LSB_1_67), .e(LSB_4_67), .d(LSB_3_67), .c(LSB_2_67));  // open: dp
  zero zero_1 (.out_1({LSB_6_67, LSB_5_67, LSB_4_67, LSB_3_67, LSB_2_67, LSB_1_67, LSB_0_67}));
  base_select_3_sure_0 base_select_3_sure_0_1 (
    .in_1(operation_1_out_4[4]), .in_2(Base_Selector),
    .out_3({LSB_6_5, LSB_5_5, LSB_4_5, LSB_3_5, LSB_2_5, LSB_1_5, LSB_0_5}));
  base_select_3_sure_0 base_select_3_sure_0_2 (
    .in_1(operation_1_out_4[3]), .in_2(Base_Selector),
    .out_3({LSB_6_4, LSB_5_4, LSB_4_4, LSB_3_4, LSB_2_4, LSB_1_4, LSB_0_4}));
  base_select_3_sure_0 base_select_3_sure_0_3 (
    .in_1(operation_1_out_4[2]), .in_2(Base_Selector),
    .out_3({LSB_6_3, LSB_5_3, LSB_4_3, LSB_3_3, LSB_2_3, LSB_1_3, LSB_0_3}));
  base_select_2_LSB base_select_2_lsb_1 (
    .in_2(octal_out_2), .in_3(base9_out_2), .in_1(operation_1_out_4[1]), .in_4(Base_Selector),
    .out_5({LSB_6_2, LSB_5_2, LSB_4_2, LSB_3_2, LSB_2_2, LSB_1_2, LSB_0_2}));
  base_select_2_LSB base_select_2_lsb_2 (
    .in_2(octal_out_3), .in_3(base9_out_3), .in_1(operation_1_out_4[0]), .in_4(Base_Selector),
    .out_5({LSB_6_1, LSB_5_1, LSB_4_1, LSB_3_1, LSB_2_1, LSB_1_1, LSB_0_1}));
  _7_Segment_Display u_7_segment_display_3 (
    .g(LSB_6_5), .f(LSB_5_5), .a(LSB_0_5), .b(LSB_1_5), .e(LSB_4_5), .d(LSB_3_5), .c(LSB_2_5));  // open: dp
  _7_Segment_Display u_7_segment_display_4 (
    .g(LSB_6_4), .f(LSB_5_4), .a(LSB_0_4), .b(LSB_1_4), .e(LSB_4_4), .d(LSB_3_4), .c(LSB_2_4));  // open: dp
  _7_Segment_Display u_7_segment_display_5 (
    .g(LSB_6_3), .f(LSB_5_3), .a(LSB_0_3), .b(LSB_1_3), .e(LSB_4_3), .d(LSB_3_3), .c(LSB_2_3));  // open: dp
  _7_Segment_Display u_7_segment_display_6 (
    .g(LSB_6_2), .f(LSB_5_2), .a(LSB_0_2), .b(LSB_1_2), .e(LSB_4_2), .d(LSB_3_2), .c(LSB_2_2));  // open: dp
  _7_Segment_Display u_7_segment_display_7 (
    .g(LSB_6_1), .f(LSB_5_1), .a(LSB_0_1), .b(LSB_1_1), .e(LSB_4_1), .d(LSB_3_1), .c(LSB_2_1));  // open: dp

  // Other names for the same wires on the sheet: A_C = Operation; base[1:0] = Base_Selector

  // Notes on the sheet:
  //   00 - Binary
  //   01 - Octal
  //   10 - Base 9
  //   0 - Adder
  //   1 - Comparator
endmodule

module Convert_to_octal (
  input  C,
  input  B,
  input  A,
  output a_2,
  output b_2,
  output c_2,
  output d,
  output e,
  output f,
  output g
);

  wire n7404_1_p4, n7404_1_p5, n7404_1_p7, n7408_2_p7, n7432_1_p6, n7432_1_p7, n7432_1_p12, n7432_1_p13,
       n7432_2_p6, n7432_2_p7, n7432_2_p12, n7432_2_p13, n7432_3_p7, n7432_3_p12, n7432_3_p13;

  // _7404 7404_1: pin names not known; wires that end beside it: 1'b1, B, C, n7404_1_p4, n7404_1_p5, A, n7404_1_p7, 1'b0
  // _7432 7432_1: pin names not known; wires that end beside it: 1'b1, C, C, n7404_1_p4, B, n7432_1_p6, n7432_1_p7, n7404_1_p4, B, n7404_1_p5, n7404_1_p5, n7432_1_p12, n7432_1_p13, 1'b0
  // _7432 7432_2: pin names not known; wires that end beside it: 1'b1, A, C, n7432_1_p13, n7404_1_p7, n7432_2_p6, n7432_2_p7, n7404_1_p7, n7404_1_p4, n7432_1_p7, n7404_1_p7, n7432_2_p12, n7432_2_p13, 1'b0
  // _7432 7432_3: pin names not known; wires that end beside it: 1'b1, n7432_1_p6, n7432_1_p13, A, n7404_1_p7, c_2, n7432_3_p7, n7432_1_p12, n7432_1_p12, n7404_1_p7, A, n7432_3_p12, n7432_3_p13, 1'b0
  // _7408 7408_1: pin names not known; wires that end beside it: 1'b1, a_2, n7432_2_p12, n7432_3_p12, n7432_2_p6, d, a_2, n7404_1_p7, n7432_3_p7, n7432_1_p13, n7432_3_p13, e, b_2, 1'b0
  // _7408 7408_2: pin names not known; wires that end beside it: 1'b1, n7432_1_p7, n7432_2_p7, n7432_3_p12, n7432_1_p6, g, n7408_2_p7, n7408_2_p7, n7432_2_p13, f, 1'b0
  _7_Segment_Display u_7_segment_display_1 (.g(g), .f(f), .a(a_2), .b(b_2), .e(e), .d(d), .c(c_2));  // open: dp
endmodule

module convert_to_octal__all (
  input  [4:0] in_1,
  output [6:0] out_2,
  output [6:0] out_3
);

  Convert_to_octal convert_to_octal_1 (
    .C(1'b0), .B(in_1[4]), .A(in_1[3]), .a_2(out_2[0]), .b_2(out_2[1]), .c_2(out_2[2]), .d(out_2[3]),
    .e(out_2[4]), .f(out_2[5]), .g(out_2[6]));
  Convert_to_octal convert_to_octal_2 (
    .C(in_1[2]), .B(in_1[1]), .A(in_1[0]), .a_2(out_3[0]), .b_2(out_3[1]), .c_2(out_3[2]), .d(out_3[3]),
    .e(out_3[4]), .f(out_3[5]), .g(out_3[6]));
endmodule

module convert_to_base9_1 (
  input  A,
  input  B,
  input  C,
  input  D,
  input  E,
  output a1,
  output b1,
  output c1,
  output d1,
  output e1,
  output f1,
  output g1
);

  wire and_1_out, and_2_out, and_3_out, and_4_out, and_5_out, and_6_out, and_7_out, and_8_out, and_9_out,
       and_10_out, and_11_out, and_12_out, and_13_out, and_14_out, and_15_out, and_16_out, and_17_out,
       and_18_out, and_19_out, and_20_out, and_21_out, and_22_out, and_23_out, and_24_out, not_1_out,
       not_2_out, not_3_out, not_4_out, not_5_out, not_6_out, not_7_out, not_8_out, not_9_out, not_10_out,
       not_11_out, not_12_out, not_13_out, not_14_out, not_15_out, not_16_out, not_17_out, not_18_out,
       not_19_out, not_20_out, not_21_out, not_22_out, not_23_out, not_24_out, not_25_out, not_26_out,
       not_27_out, not_28_out, not_29_out, not_30_out, not_31_out, not_32_out, not_33_out, not_34_out,
       not_35_out, not_36_out, not_37_out, not_38_out;

  not not_1 (not_1_out, A);
  not not_2 (not_2_out, B);
  not not_3 (not_3_out, A);
  not not_4 (not_4_out, C);
  not not_5 (not_5_out, D);
  not not_6 (not_6_out, E);
  not not_7 (not_7_out, B);
  not not_8 (not_8_out, B);
  not not_9 (not_9_out, B);
  not not_10 (not_10_out, C);
  not not_11 (not_11_out, D);
  not not_12 (not_12_out, A);
  not not_13 (not_13_out, B);
  not not_14 (not_14_out, A);
  not not_15 (not_15_out, C);
  not not_16 (not_16_out, D);
  not not_17 (not_17_out, E);
  not not_18 (not_18_out, B);
  not not_19 (not_19_out, B);
  not not_20 (not_20_out, A);
  not not_21 (not_21_out, B);
  not not_22 (not_22_out, A);
  not not_23 (not_23_out, C);
  not not_24 (not_24_out, D);
  not not_25 (not_25_out, E);
  not not_26 (not_26_out, B);
  not not_27 (not_27_out, B);
  not not_28 (not_28_out, C);
  not not_29 (not_29_out, D);
  not not_30 (not_30_out, C);
  not not_31 (not_31_out, E);
  not not_32 (not_32_out, A);
  not not_33 (not_33_out, B);
  not not_34 (not_34_out, A);
  not not_35 (not_35_out, C);
  not not_36 (not_36_out, D);
  not not_37 (not_37_out, E);
  and and_1 (and_1_out, A, D);
  and and_2 (and_2_out, A, C);
  and and_3 (and_3_out, A, B);
  and and_4 (and_4_out, not_1_out, not_2_out);
  and and_5 (and_5_out, not_3_out, not_4_out, not_5_out, not_6_out);
  and and_6 (and_6_out, not_7_out, D);
  and and_7 (and_7_out, not_8_out, C);
  and and_8 (and_8_out, A, B);
  not not_38 (not_38_out, A);
  and and_9 (and_9_out, not_9_out, not_10_out, not_11_out);
  and and_10 (and_10_out, B, D, E);
  and and_11 (and_11_out, B, C);
  and and_12 (and_12_out, not_12_out, not_13_out);
  and and_13 (and_13_out, not_14_out, not_15_out, not_16_out, not_17_out);
  and and_14 (and_14_out, not_18_out, D);
  and and_15 (and_15_out, not_19_out, C);
  and and_16 (and_16_out, A, B);
  and and_17 (and_17_out, not_20_out, not_21_out);
  and and_18 (and_18_out, not_22_out, not_23_out, not_24_out, not_25_out);
  and and_19 (and_19_out, not_26_out, D);
  and and_20 (and_20_out, not_27_out, C);
  and and_21 (and_21_out, A, B, not_28_out, not_29_out);
  and and_22 (and_22_out, A, B, not_30_out, not_31_out);
  and and_23 (and_23_out, not_32_out, not_33_out);
  and and_24 (and_24_out, not_34_out, not_35_out, not_36_out, not_37_out);
  or or_1 (g1, and_1_out, and_2_out, and_3_out);
  or or_2 (a1, and_4_out, and_5_out, and_6_out, and_7_out, and_8_out);
  or or_3 (c1, not_38_out, and_9_out, and_10_out, and_11_out);
  or or_4 (d1, and_12_out, and_13_out, and_14_out, and_15_out, and_16_out);
  or or_5 (e1, and_17_out, and_18_out, and_19_out, and_20_out, and_21_out, and_22_out);
  or or_6 (f1, and_23_out, and_24_out);

  assign b1 = 1'b1;
endmodule

module convert_to_base9_0 (
  input  A,
  input  B,
  input  C,
  input  D,
  input  E,
  output a2,
  output b2,
  output c2,
  output d2,
  output e2,
  output f2,
  output g2
);

  wire and_1_out, and_2_out, and_3_out, and_4_out, and_5_out, and_6_out, and_7_out, and_8_out, and_9_out,
       and_10_out, and_11_out, and_12_out, and_13_out, and_14_out, and_15_out, and_16_out, and_17_out,
       and_18_out, and_19_out, and_20_out, and_21_out, and_22_out, and_23_out, and_24_out, and_25_out,
       and_26_out, and_27_out, and_28_out, and_29_out, and_30_out, and_31_out, and_32_out, and_33_out,
       and_34_out, and_35_out, and_36_out, and_37_out, and_38_out, and_39_out, and_40_out, and_41_out,
       and_42_out, and_43_out, and_44_out, and_45_out, and_46_out, and_47_out, and_48_out, and_49_out,
       and_50_out, and_51_out, and_52_out, and_53_out, and_54_out, and_55_out, and_56_out, and_57_out,
       and_58_out, and_59_out, and_60_out, and_61_out, and_62_out, and_63_out, and_64_out, not_1_out,
       not_2_out, not_3_out, not_4_out, not_5_out, not_6_out, not_7_out, not_8_out, not_9_out, not_10_out,
       not_11_out, not_12_out, not_13_out, not_14_out, not_15_out, not_16_out, not_17_out, not_18_out,
       not_19_out, not_20_out, not_21_out, not_22_out, not_23_out, not_24_out, not_25_out, not_26_out,
       not_27_out, not_28_out, not_29_out, not_30_out, not_31_out, not_32_out, not_33_out, not_34_out,
       not_35_out, not_36_out, not_37_out, not_38_out, not_39_out, not_40_out, not_41_out, not_42_out,
       not_43_out, not_44_out, not_45_out, not_46_out, not_47_out, not_48_out, not_49_out, not_50_out,
       not_51_out, not_52_out, not_53_out, not_54_out, not_55_out, not_56_out, not_57_out, not_58_out,
       not_59_out, not_60_out, not_61_out, not_62_out, not_63_out, not_64_out, not_65_out, not_66_out,
       not_67_out, not_68_out, not_69_out, not_70_out, not_71_out, not_72_out, not_73_out, not_74_out,
       not_75_out, not_76_out, not_77_out, not_78_out, not_79_out, not_80_out, not_81_out, not_82_out,
       not_83_out, not_84_out, not_85_out, not_86_out, not_87_out, not_88_out, not_89_out, not_90_out,
       not_91_out, not_92_out, not_93_out, not_94_out, not_95_out, not_96_out, not_97_out, not_98_out,
       not_99_out, not_100_out, not_101_out, not_102_out, not_103_out, not_104_out, not_105_out, not_106_out,
       not_107_out, not_108_out, not_109_out, not_110_out, not_111_out, not_112_out, not_113_out,
       not_114_out, not_115_out, not_116_out, not_117_out, not_118_out, not_119_out;

  not not_1 (not_1_out, B);
  not not_2 (not_2_out, C);
  not not_3 (not_3_out, E);
  not not_4 (not_4_out, A);
  not not_5 (not_5_out, B);
  not not_6 (not_6_out, A);
  not not_7 (not_7_out, B);
  not not_8 (not_8_out, A);
  not not_9 (not_9_out, A);
  not not_10 (not_10_out, D);
  not not_11 (not_11_out, E);
  not not_12 (not_12_out, C);
  not not_13 (not_13_out, D);
  not not_14 (not_14_out, B);
  not not_15 (not_15_out, D);
  not not_16 (not_16_out, D);
  not not_17 (not_17_out, A);
  not not_18 (not_18_out, C);
  not not_19 (not_19_out, B);
  not not_20 (not_20_out, C);
  not not_21 (not_21_out, C);
  not not_22 (not_22_out, A);
  not not_23 (not_23_out, B);
  not not_24 (not_24_out, D);
  not not_25 (not_25_out, E);
  not not_26 (not_26_out, A);
  not not_27 (not_27_out, D);
  not not_28 (not_28_out, D);
  not not_29 (not_29_out, E);
  not not_30 (not_30_out, C);
  not not_31 (not_31_out, D);
  not not_32 (not_32_out, B);
  not not_33 (not_33_out, A);
  not not_34 (not_34_out, E);
  not not_35 (not_35_out, A);
  not not_36 (not_36_out, B);
  not not_37 (not_37_out, C);
  not not_38 (not_38_out, E);
  not not_39 (not_39_out, A);
  not not_40 (not_40_out, B);
  not not_41 (not_41_out, E);
  not not_42 (not_42_out, B);
  not not_43 (not_43_out, C);
  not not_44 (not_44_out, E);
  not not_45 (not_45_out, A);
  not not_46 (not_46_out, C);
  not not_47 (not_47_out, B);
  not not_48 (not_48_out, D);
  not not_49 (not_49_out, A);
  not not_50 (not_50_out, C);
  not not_51 (not_51_out, D);
  not not_52 (not_52_out, A);
  not not_53 (not_53_out, D);
  not not_54 (not_54_out, E);
  not not_55 (not_55_out, C);
  not not_56 (not_56_out, D);
  not not_57 (not_57_out, E);
  not not_58 (not_58_out, B);
  not not_59 (not_59_out, D);
  not not_60 (not_60_out, B);
  not not_61 (not_61_out, D);
  not not_62 (not_62_out, A);
  not not_63 (not_63_out, C);
  not not_64 (not_64_out, D);
  not not_65 (not_65_out, E);
  not not_66 (not_66_out, A);
  not not_67 (not_67_out, B);
  not not_68 (not_68_out, E);
  not not_69 (not_69_out, B);
  not not_70 (not_70_out, C);
  not not_71 (not_71_out, E);
  not not_72 (not_72_out, A);
  not not_73 (not_73_out, C);
  not not_74 (not_74_out, D);
  not not_75 (not_75_out, B);
  not not_76 (not_76_out, C);
  not not_77 (not_77_out, D);
  not not_78 (not_78_out, B);
  not not_79 (not_79_out, D);
  not not_80 (not_80_out, E);
  not not_81 (not_81_out, C);
  not not_82 (not_82_out, E);
  not not_83 (not_83_out, A);
  not not_84 (not_84_out, B);
  not not_85 (not_85_out, D);
  not not_86 (not_86_out, E);
  not not_87 (not_87_out, A);
  not not_88 (not_88_out, D);
  not not_89 (not_89_out, A);
  not not_90 (not_90_out, E);
  not not_91 (not_91_out, A);
  not not_92 (not_92_out, C);
  not not_93 (not_93_out, D);
  not not_94 (not_94_out, A);
  not not_95 (not_95_out, B);
  not not_96 (not_96_out, C);
  not not_97 (not_97_out, D);
  not not_98 (not_98_out, B);
  not not_99 (not_99_out, E);
  not not_100 (not_100_out, B);
  not not_101 (not_101_out, C);
  not not_102 (not_102_out, E);
  not not_103 (not_103_out, C);
  not not_104 (not_104_out, A);
  not not_105 (not_105_out, B);
  not not_106 (not_106_out, C);
  not not_107 (not_107_out, A);
  not not_108 (not_108_out, C);
  not not_109 (not_109_out, A);
  not not_110 (not_110_out, D);
  not not_111 (not_111_out, E);
  not not_112 (not_112_out, C);
  not not_113 (not_113_out, D);
  not not_114 (not_114_out, E);
  not not_115 (not_115_out, B);
  not not_116 (not_116_out, D);
  not not_117 (not_117_out, B);
  not not_118 (not_118_out, C);
  not not_119 (not_119_out, E);
  and and_1 (and_1_out, not_1_out, not_2_out, not_3_out);
  and and_2 (and_2_out, not_4_out, not_5_out, D);
  and and_3 (and_3_out, not_6_out, D, E);
  and and_4 (and_4_out, not_7_out, C, E);
  and and_5 (and_5_out, not_8_out, C, D);
  and and_6 (and_6_out, not_9_out, B, not_10_out, not_11_out);
  and and_7 (and_7_out, B, not_12_out, not_13_out);
  and and_8 (and_8_out, A, not_14_out, not_15_out);
  and and_9 (and_9_out, A, not_16_out, E);
  and and_10 (and_10_out, A, B, D);
  and and_11 (and_11_out, not_17_out, not_18_out);
  and and_12 (and_12_out, not_19_out, not_20_out);
  and and_13 (and_13_out, not_21_out, D);
  and and_14 (and_14_out, not_22_out, not_23_out, D, E);
  and and_15 (and_15_out, C, not_24_out, not_25_out);
  and and_16 (and_16_out, not_26_out, B, not_27_out);
  and and_17 (and_17_out, A, not_28_out, E);
  and and_18 (and_18_out, A, D, not_29_out);
  and and_19 (and_19_out, not_30_out, not_31_out);
  and and_20 (and_20_out, not_32_out, E);
  and and_21 (and_21_out, not_33_out, C);
  and and_22 (and_22_out, B, not_34_out);
  and and_23 (and_23_out, A, D);
  and and_24 (and_24_out, not_35_out, not_36_out, not_37_out, not_38_out);
  and and_25 (and_25_out, not_39_out, not_40_out, D, not_41_out);
  and and_26 (and_26_out, not_42_out, not_43_out, D, not_44_out);
  and and_27 (and_27_out, not_45_out, not_46_out, D, E);
  and and_28 (and_28_out, not_47_out, C, not_48_out, E);
  and and_29 (and_29_out, not_49_out, B, not_50_out, not_51_out);
  and and_30 (and_30_out, not_52_out, B, not_53_out, not_54_out);
  and and_31 (and_31_out, B, not_55_out, not_56_out, not_57_out);
  and and_32 (and_32_out, B, C, D);
  and and_33 (and_33_out, A, not_58_out, not_59_out, E);
  and and_34 (and_34_out, A, not_60_out, C, not_61_out);
  and and_35 (and_35_out, A, C, E);
  and and_36 (and_36_out, A, B, D);
  and and_37 (and_37_out, not_62_out, not_63_out, not_64_out, not_65_out);
  and and_38 (and_38_out, not_66_out, not_67_out, D, not_68_out);
  and and_39 (and_39_out, not_69_out, not_70_out, D, not_71_out);
  and and_40 (and_40_out, not_72_out, B, not_73_out, not_74_out);
  and and_41 (and_41_out, B, D, E);
  and and_42 (and_42_out, A, not_75_out, not_76_out, not_77_out, E);
  and and_43 (and_43_out, A, not_78_out, C, not_79_out, not_80_out);
  and and_44 (and_44_out, A, B, not_81_out, not_82_out);
  and and_45 (and_45_out, A, B, C, E);
  and and_46 (and_46_out, not_83_out, not_84_out, not_85_out, not_86_out);
  and and_47 (and_47_out, not_87_out, C, not_88_out, E);
  and and_48 (and_48_out, not_89_out, C, D, not_90_out);
  and and_49 (and_49_out, not_91_out, B, not_92_out, not_93_out);
  and and_50 (and_50_out, not_94_out, B, C, D);
  and and_51 (and_51_out, A, not_95_out, not_96_out, not_97_out, E);
  and and_52 (and_52_out, A, not_98_out, D, not_99_out);
  and and_53 (and_53_out, A, not_100_out, C, D);
  and and_54 (and_54_out, A, B, not_101_out, not_102_out);
  and and_55 (and_55_out, A, B, not_103_out, D);
  and and_56 (and_56_out, not_104_out, not_105_out, not_106_out, D);
  and and_57 (and_57_out, not_107_out, not_108_out, D, E);
  and and_58 (and_58_out, not_109_out, C, not_110_out);
  and and_59 (and_59_out, C, D, not_111_out);
  and and_60 (and_60_out, B, not_112_out, not_113_out, not_114_out);
  and and_61 (and_61_out, B, C, E);
  and and_62 (and_62_out, A, not_115_out, not_116_out, E);
  and and_63 (and_63_out, A, not_117_out, C);
  and and_64 (and_64_out, A, B, not_118_out, not_119_out);
  or or_1 (a2, and_1_out, and_2_out, and_3_out, and_4_out, and_5_out, and_6_out, and_7_out, and_8_out, and_9_out, and_10_out);
  or or_2 (b2, and_11_out, and_12_out, and_13_out, and_14_out, and_15_out, and_16_out, and_17_out, and_18_out);
  or or_3 (c2, and_19_out, and_20_out, and_21_out, and_22_out, and_23_out);
  or or_4 (d2, and_24_out, and_25_out, and_26_out, and_27_out, and_28_out, and_29_out, and_30_out, and_31_out, and_32_out, and_33_out, and_34_out, and_35_out, and_36_out);
  or or_5 (e2, and_37_out, and_38_out, and_39_out, and_40_out, and_41_out, and_42_out, and_43_out, and_44_out, and_45_out);
  or or_6 (f2, and_46_out, and_47_out, and_48_out, and_49_out, and_50_out, and_51_out, and_52_out, and_53_out, and_54_out, and_55_out);
  or or_7 (g2, and_56_out, and_57_out, and_58_out, and_59_out, and_60_out, and_61_out, and_62_out, and_63_out, and_64_out);
endmodule

module convert_to_base9__all (
  input  [4:0] in_1,
  output [6:0] out_2,
  output [6:0] out_3
);

  convert_to_base9_1 convert_to_base9_1_1 (
    .A(in_1[4]), .B(in_1[3]), .C(in_1[2]), .D(in_1[1]), .E(in_1[0]), .a1(out_2[0]), .b1(out_2[1]),
    .c1(out_2[2]), .d1(out_2[3]), .e1(out_2[4]), .f1(out_2[5]), .g1(out_2[6]));
  convert_to_base9_0 convert_to_base9_0_1 (
    .A(in_1[4]), .B(in_1[3]), .C(in_1[2]), .D(in_1[1]), .E(in_1[0]), .a2(out_3[0]), .b2(out_3[1]),
    .c2(out_3[2]), .d2(out_3[3]), .e2(out_3[4]), .f2(out_3[5]), .g2(out_3[6]));
endmodule

module zero (
  output [6:0] out_1
);


  assign out_1 = 7'b0111111;
endmodule

module one (
  output [6:0] out_1
);


  assign out_1 = 7'b0000110;
endmodule

module base_select_2_LSB (
  input  in_1,
  input  [6:0] in_2,
  input  [6:0] in_3,
  input  [1:0] in_4,
  output [6:0] out_5
);

  wire [6:0] multiplexer_1_out, one_1_out_1, zero_1_out_1;

  zero zero_1 (.out_1(zero_1_out_1));
  one one_1 (.out_1(one_1_out_1));
  Multiplexer #(.width(7)) multiplexer_1 (
    .in0(zero_1_out_1), .in1(one_1_out_1), .out(multiplexer_1_out), .sel(in_1));  // open: en
  Multiplexer #(.select(2), .width(7)) multiplexer_2 (
    .in0(multiplexer_1_out), .in1(in_2), .in2(in_3), .out(out_5), .sel(in_4));  // open: in3, en
endmodule

module base_select_3_sure_0 (
  input  in_1,
  input  [1:0] in_2,
  output [6:0] out_3
);

  wire [6:0] multiplexer_1_out, one_1_out_1, zero_1_out_1;

  zero zero_1 (.out_1(zero_1_out_1));
  one one_1 (.out_1(one_1_out_1));
  Multiplexer #(.width(7)) multiplexer_1 (
    .in0(zero_1_out_1), .in1(one_1_out_1), .out(multiplexer_1_out), .sel(in_1));  // open: en
  Multiplexer #(.select(2), .width(7)) multiplexer_2 (
    .in0(multiplexer_1_out), .in1(zero_1_out_1), .in2(zero_1_out_1), .out(out_3), .sel(in_2));  // open: in3, en
endmodule

module Operation (
  input  [3:0] Input_1,
  input  [3:0] Input_2,
  input  Operation,
  output [4:0] out_4
);

  wire comparator_1_eq, comparator_1_gt, comparator_1_lt;
  wire [3:0] multiplexer_1_out, multiplexer_2_out;
  wire [4:0] bit_extender_1_out, bit_extender_2_out, bit_extender_5_out, C, D;

  assign bit_extender_1_out = {{1{1'b0}}, Input_1};  // Bit_Extender bit_extender_1
  assign bit_extender_2_out = {{1{1'b0}}, Input_2};  // Bit_Extender bit_extender_2
  Comparator #(.width(4), .mode("unsigned")) comparator_1 (
    .a(Input_1), .b(Input_2), .gt(comparator_1_gt), .eq(comparator_1_eq), .lt(comparator_1_lt));
  Adder #(.width(5)) adder_1 (.a(bit_extender_1_out), .b(bit_extender_2_out), .out(C));  // open: cin, cout
  Multiplexer #(.width(4)) multiplexer_1 (
    .in1(Input_1), .out(multiplexer_1_out), .sel(comparator_1_gt), .en(1'b1));  // open: in0
  Multiplexer #(.width(4)) multiplexer_2 (
    .in1(Input_2), .out(multiplexer_2_out), .sel(comparator_1_lt), .en(1'b1));  // open: in0
  Multiplexer #(.width(5)) multiplexer_3 (.in0(C), .in1(D), .out(out_4), .sel(Operation), .en(1'b1));
  assign D = {{1{1'b0}}, multiplexer_1_out};  // Bit_Extender bit_extender_3
  assign D = {{1{1'b0}}, multiplexer_2_out};  // Bit_Extender bit_extender_4
  assign bit_extender_5_out = {{4{1'b0}}, 1'b0};  // Bit_Extender bit_extender_5
  Multiplexer #(.width(5)) multiplexer_4 (
    .in1(bit_extender_5_out), .out(D), .sel(comparator_1_eq), .en(1'b1));  // open: in0

  // Other names for the same wires on the sheet: A[3:0] = Input_1; B[3:0] = Input_2; O = Operation

  // Notes on the sheet:
  //   Adder
  //   Comparator
  //   Output
endmodule
