// Logisim project Project 2.circ as structural Verilog: 3 circuits, main circuit main
module main (
  input  Mode_Selector
);

  wire LED, M_minus, M_plus, main_subcircuit_1_pause_led, main_subcircuit_1_pause_led_2, n6bit_rom_1_out_3,
       n6bit_rom_1_out_4, n6bit_rom_1_out_5, n6bit_rom_1_out_6, n6bit_rom_1_out_7, n6bit_rom_1_out_8,
       n6bit_rom_1_out_9, n6bit_rom_1_out_10, n6bit_rom_1_out_11, n6bit_rom_1_out_12, n6bit_rom_1_out_13,
       n6bit_rom_1_out_14, n6bit_rom_1_out_15, n6bit_rom_1_out_16, n6bit_rom_2_out_3, n6bit_rom_2_out_4,
       n6bit_rom_2_out_5, n6bit_rom_2_out_6, n6bit_rom_2_out_7, n6bit_rom_2_out_8, n6bit_rom_2_out_9,
       n6bit_rom_2_out_10, n6bit_rom_2_out_11, n6bit_rom_2_out_12, n6bit_rom_2_out_13, n6bit_rom_2_out_14,
       n6bit_rom_2_out_15, n6bit_rom_2_out_16, pause, play, reset, S_minus, S_plus;
  wire [5:0] Minutes, Seconds;

  _6bit_ROM u_6bit_rom_1 (
    .in_1(Minutes), .in_2(Minutes), .out_3(n6bit_rom_1_out_3), .out_4(n6bit_rom_1_out_4),
    .out_5(n6bit_rom_1_out_5), .out_6(n6bit_rom_1_out_6), .out_7(n6bit_rom_1_out_7),
    .out_8(n6bit_rom_1_out_8), .out_9(n6bit_rom_1_out_9), .out_10(n6bit_rom_1_out_10),
    .out_11(n6bit_rom_1_out_11), .out_12(n6bit_rom_1_out_12), .out_13(n6bit_rom_1_out_13),
    .out_14(n6bit_rom_1_out_14), .out_15(n6bit_rom_1_out_15), .out_16(n6bit_rom_1_out_16));
  _7_Segment_Display u_7_segment_display_1 (
    .g(n6bit_rom_1_out_16), .f(n6bit_rom_1_out_15), .a(n6bit_rom_1_out_10), .b(n6bit_rom_1_out_11),
    .e(n6bit_rom_1_out_14), .d(n6bit_rom_1_out_13), .c(n6bit_rom_1_out_12));  // open: dp
  _7_Segment_Display u_7_segment_display_2 (
    .g(n6bit_rom_1_out_9), .f(n6bit_rom_1_out_8), .a(n6bit_rom_1_out_3), .b(n6bit_rom_1_out_4),
    .e(n6bit_rom_1_out_7), .d(n6bit_rom_1_out_6), .c(n6bit_rom_1_out_5));  // open: dp
  Button Minutes_increment_button (.out(M_plus));
  Button Seconds_increment_button (.out(S_plus));
  Button Minutes_decrement_button (.out(M_minus));
  Button Seconds_decrement_button (.out(S_minus));
  Button Play_Button (.out(play));
  Button Pause_Button (.out(pause));
  Button Reset_Button (.out(reset));
  _6bit_ROM u_6bit_rom_2 (
    .in_1(Seconds), .in_2(Seconds), .out_3(n6bit_rom_2_out_3), .out_4(n6bit_rom_2_out_4),
    .out_5(n6bit_rom_2_out_5), .out_6(n6bit_rom_2_out_6), .out_7(n6bit_rom_2_out_7),
    .out_8(n6bit_rom_2_out_8), .out_9(n6bit_rom_2_out_9), .out_10(n6bit_rom_2_out_10),
    .out_11(n6bit_rom_2_out_11), .out_12(n6bit_rom_2_out_12), .out_13(n6bit_rom_2_out_13),
    .out_14(n6bit_rom_2_out_14), .out_15(n6bit_rom_2_out_15), .out_16(n6bit_rom_2_out_16));
  _7_Segment_Display u_7_segment_display_3 (
    .g(n6bit_rom_2_out_16), .f(n6bit_rom_2_out_15), .a(n6bit_rom_2_out_10), .b(n6bit_rom_2_out_11),
    .e(n6bit_rom_2_out_14), .d(n6bit_rom_2_out_13), .c(n6bit_rom_2_out_12));  // open: dp
  _7_Segment_Display u_7_segment_display_4 (
    .g(n6bit_rom_2_out_9), .f(n6bit_rom_2_out_8), .a(n6bit_rom_2_out_3), .b(n6bit_rom_2_out_4),
    .e(n6bit_rom_2_out_7), .d(n6bit_rom_2_out_6), .c(n6bit_rom_2_out_5));  // open: dp
  LED Pause_LED (.in(LED));
  Main_Subcircuit main_subcircuit_1 (
    .S_plus(S_plus), .M_plus(M_plus), .play(play), .pause(pause), .S_minus(S_minus), .M_minus(M_minus),
    .reset_input(reset), .play_2(play), .pause_led_2(main_subcircuit_1_pause_led_2),
    .pause_led(main_subcircuit_1_pause_led), .mode_2(Mode_Selector), .mode(Mode_Selector), .S(Seconds),
    .M(Minutes));
  or or_1 (LED, main_subcircuit_1_pause_led, main_subcircuit_1_pause_led_2);

  // Other names for the same wires on the sheet: mode = Mode_Selector

  // Notes on the sheet:
  //   Minutes Component
  //   Seconds Component
endmodule

module _6bit_ROM (
  input  [5:0] in_1,
  input  [5:0] in_2,
  output out_3,
  output out_4,
  output out_5,
  output out_6,
  output out_7,
  output out_8,
  output out_9,
  output out_10,
  output out_11,
  output out_12,
  output out_13,
  output out_14,
  output out_15,
  output out_16
);

  wire [7:0] rom_1_data, rom_2_data;

  ROM #(.addrWidth(6)) rom_1 (.addr(in_1), .data(rom_1_data));  // open: sel
  ROM #(.addrWidth(6)) rom_2 (.addr(in_2), .data(rom_2_data));  // open: sel
  // _7_segment_display_driver 7_segment_display_driver_1: pin names not known; wires that end beside it: rom_1_data[3], rom_1_data[2], rom_1_data[1], rom_1_data[0], out_3, out_4, out_5, out_6, out_7, out_8, out_9
  // _7_segment_display_driver 7_segment_display_driver_2: pin names not known; wires that end beside it: rom_2_data[3], rom_2_data[2], rom_2_data[1], rom_2_data[0], out_10, out_11, out_12, out_13, out_14, out_15, out_16

  // Notes on the sheet:
  //   contents of rom_1 (hex, n*v repeats v):
  //   0 1 2 3 4 5 6 7 8 9 0 1 2 3 4 5 6 7 8 9 0 1 2 3 4 5 6 7 8 9 0 1 2 3 4 5 6 7 8 9 0 1 2 3 4 5 6 7 8 9
  //   0 1 2 3 4 5 6 7 8 9
  //   contents of rom_2 (hex, n*v repeats v):
  //   10*0 10*1 10*2 10*3 10*4 10*5
endmodule

module Main_Subcircuit (
  input  S_plus,
  input  M_plus,
  input  play,
  input  mode,
  input  pause,
  input  S_minus,
  input  M_minus,
  input  reset_input,
  input  play_2,
  input  mode_2,
  output pause_led,
  output [5:0] S,
  output [5:0] M,
  output pause_led_2
);

  wire _00_00, _00_min, _00_min_t, _00_sec, _0to1, _1to0, _59_59, _59_min, _59_min_t, _59_sec, _60_min,
       _60_min_t, _60_sec, _60_sec_t, and_1_out, and_2_out, and_3_out, and_4_out, and_5_out, and_6_out,
       and_7_out, and_8_out, and_9_out, and_10_out, and_11_out, and_12_out, clock_1_out, clock_2_out,
       d_ff_1_q, d_ff_1_qn, d_ff_2_q, d_ff_2_qn, d_ff_5_qn, d_ff_6_qn, d_ff_7_qn, d_ff_8_qn, d_ff_9_qn,
       d_ff_10_qn, d_ff_11_qn, d_ff_12_qn, d_ff_13_qn, d_ff_14_qn, d_ff_15_qn, d_ff_16_qn, d_ff_17_qn,
       d_ff_18_qn, d_ff_19_qn, d_ff_20_qn, d_ff_21_qn, d_ff_22_qn, d_ff_23_qn, d_ff_24_qn, d_ff_25_qn,
       d_ff_26_qn, d_ff_27_qn, d_ff_28_qn, M_minus_minus, M_plus_plus, M_yes, M_yes_t, min00, not_1_out,
       not_2_out, not_5_out, not_6_out, or_1_out, or_2_out, or_6_out, or_8_out, or_9_out, or_12_out,
       or_13_out, p, p0, p59, PauseCheck, RESET, reset1, reset2, reset3, S_yes, S_yes_t;
  wire [5:0] d_ff_5_q, d_ff_11_q, d_ff_17_q, d_ff_23_q;

  not not_1 (not_1_out, p0);
  and and_1 (and_1_out, play, not_2_out);
  not not_2 (not_2_out, p59);
  Clock clock_1 (.out(clock_1_out));
  and and_2 (and_2_out, play_2, not_1_out);
  Clock clock_2 (.out(clock_2_out));
  D_Flip_Flop d_ff_1 (
    .clk(or_1_out), .D(d_ff_1_qn), .Q(d_ff_1_q), .Qn(d_ff_1_qn), .preset(and_1_out), .reset(p));  // open: en
  not not_3 (pause_led, d_ff_1_q);
  or or_1 (or_1_out, and_1_out, mode, p);
  and and_3 (and_3_out, clock_1_out, d_ff_2_q);
  D_Flip_Flop d_ff_2 (
    .clk(or_2_out), .D(d_ff_2_qn), .Q(d_ff_2_q), .Qn(d_ff_2_qn), .preset(and_2_out), .reset(p));  // open: en
  not not_4 (pause_led_2, d_ff_2_q);
  or or_2 (or_2_out, and_2_out, mode, p);
  not not_5 (not_5_out, mode);
  and and_4 (and_4_out, clock_2_out, d_ff_1_q);
  not not_6 (not_6_out, mode);
  or or_3 (PauseCheck, pause_led, pause_led_2);
  or or_4 (p, _1to0, RESET, _00_00, _59_59, pause, _0to1);
  D_Flip_Flop d_ff_3 (.clk(mode), .D(mode), .Q(_0to1), .reset(and_5_out));  // open: Qn, preset, en
  and and_5 (and_5_out, mode, _0to1);
  D_Flip_Flop d_ff_4 (.clk(not_5_out), .D(not_5_out), .Q(_1to0), .reset(and_6_out));  // open: Qn, preset, en
  and and_6 (and_6_out, not_5_out, _1to0);
  and and_7 (and_7_out, and_4_out, not_6_out);
  and and_8 (and_8_out, and_3_out, mode);
  and and_9 (and_9_out, S_plus, PauseCheck);
  and and_10 (and_10_out, S_minus, PauseCheck);
  or or_5 (S_yes, and_9_out, and_7_out);
  or or_6 (or_6_out, or_8_out, M_minus_minus);
  or or_7 (S_yes_t, and_10_out, and_8_out);
  D_Flip_Flop d_ff_5 (
    .clk(S_yes), .D(d_ff_5_qn), .Q(d_ff_5_q[0]), .Qn(d_ff_5_qn), .preset(M_minus_minus), .reset(or_8_out));  // open: en
  D_Flip_Flop d_ff_6 (
    .clk(d_ff_5_qn), .D(d_ff_6_qn), .Q(d_ff_5_q[1]), .Qn(d_ff_6_qn), .preset(M_minus_minus), .reset(or_8_out));  // open: en
  D_Flip_Flop d_ff_7 (
    .clk(d_ff_6_qn), .D(d_ff_7_qn), .Q(d_ff_5_q[2]), .Qn(d_ff_7_qn), .reset(or_6_out));  // open: preset, en
  D_Flip_Flop d_ff_8 (
    .clk(d_ff_7_qn), .D(d_ff_8_qn), .Q(d_ff_5_q[3]), .Qn(d_ff_8_qn), .preset(M_minus_minus), .reset(or_8_out));  // open: en
  D_Flip_Flop d_ff_9 (
    .clk(d_ff_8_qn), .D(d_ff_9_qn), .Q(d_ff_5_q[4]), .Qn(d_ff_9_qn), .preset(M_minus_minus), .reset(or_8_out));  // open: en
  D_Flip_Flop d_ff_10 (
    .clk(d_ff_9_qn), .D(d_ff_10_qn), .Q(d_ff_5_q[5]), .Qn(d_ff_10_qn), .preset(M_minus_minus),
    .reset(or_8_out));  // open: en
  D_Flip_Flop d_ff_11 (
    .clk(S_yes_t), .D(d_ff_11_qn), .Q(d_ff_11_q[0]), .Qn(d_ff_11_qn), .reset(or_9_out));  // open: preset, en
  D_Flip_Flop d_ff_12 (
    .clk(d_ff_11_qn), .D(d_ff_12_qn), .Q(d_ff_11_q[1]), .Qn(d_ff_12_qn), .reset(or_9_out));  // open: preset, en
  D_Flip_Flop d_ff_13 (
    .clk(d_ff_12_qn), .D(d_ff_13_qn), .Q(d_ff_11_q[2]), .Qn(d_ff_13_qn), .reset(or_9_out));  // open: preset, en
  D_Flip_Flop d_ff_14 (
    .clk(d_ff_13_qn), .D(d_ff_14_qn), .Q(d_ff_11_q[3]), .Qn(d_ff_14_qn), .reset(or_9_out));  // open: preset, en
  D_Flip_Flop d_ff_15 (
    .clk(d_ff_14_qn), .D(d_ff_15_qn), .Q(d_ff_11_q[4]), .Qn(d_ff_15_qn), .reset(or_9_out));  // open: preset, en
  D_Flip_Flop d_ff_16 (
    .clk(d_ff_15_qn), .D(d_ff_16_qn), .Q(d_ff_11_q[5]), .Qn(d_ff_16_qn), .reset(or_9_out));  // open: preset, en
  or or_8 (or_8_out, RESET, M_plus_plus);
  or or_9 (or_9_out, RESET, M_minus_minus, M_plus_plus);
  Subtractor #(.width(6)) subtractor_1 (.a(d_ff_5_q), .b(d_ff_11_q), .out(S));  // open: bin, bout
  Comparator #(.width(6), .mode("unsigned")) comparator_1 (.a({6{1'b0}}), .b(S), .eq(_00_sec));  // open: gt, lt
  Comparator #(.width(6), .mode("unsigned")) comparator_2 (
    .a(6'b111100), .b(S), .eq(_60_sec_t), .lt(_60_sec));  // open: gt
  Comparator #(.width(6), .mode("unsigned")) comparator_3 (.a(6'b111011), .b(S), .eq(_59_sec));  // open: gt, lt
  and and_11 (and_11_out, M_plus, PauseCheck);
  or or_10 (M_yes, and_11_out, M_plus_plus);
  and and_12 (and_12_out, M_minus, PauseCheck);
  or or_11 (M_yes_t, and_12_out, M_minus_minus);
  D_Flip_Flop d_ff_17 (
    .clk(M_yes), .D(d_ff_17_qn), .Q(d_ff_17_q[0]), .Qn(d_ff_17_qn), .reset(or_12_out));  // open: preset, en
  D_Flip_Flop d_ff_18 (
    .clk(d_ff_17_qn), .D(d_ff_18_qn), .Q(d_ff_17_q[1]), .Qn(d_ff_18_qn), .reset(or_12_out));  // open: preset, en
  D_Flip_Flop d_ff_19 (
    .clk(d_ff_18_qn), .D(d_ff_19_qn), .Q(d_ff_17_q[2]), .Qn(d_ff_19_qn), .reset(or_12_out));  // open: preset, en
  D_Flip_Flop d_ff_20 (
    .clk(d_ff_19_qn), .D(d_ff_20_qn), .Q(d_ff_17_q[3]), .Qn(d_ff_20_qn), .reset(or_12_out));  // open: preset, en
  D_Flip_Flop d_ff_21 (
    .clk(d_ff_20_qn), .D(d_ff_21_qn), .Q(d_ff_17_q[4]), .Qn(d_ff_21_qn), .reset(or_12_out));  // open: preset, en
  D_Flip_Flop d_ff_22 (
    .clk(d_ff_21_qn), .D(d_ff_22_qn), .Q(d_ff_17_q[5]), .Qn(d_ff_22_qn), .reset(or_12_out));  // open: preset, en
  or or_12 (or_12_out, RESET, min00);
  D_Flip_Flop d_ff_23 (
    .clk(M_yes_t), .D(d_ff_23_qn), .Q(d_ff_23_q[0]), .Qn(d_ff_23_qn), .reset(or_13_out));  // open: preset, en
  D_Flip_Flop d_ff_24 (
    .clk(d_ff_23_qn), .D(d_ff_24_qn), .Q(d_ff_23_q[1]), .Qn(d_ff_24_qn), .reset(or_13_out));  // open: preset, en
  D_Flip_Flop d_ff_25 (
    .clk(d_ff_24_qn), .D(d_ff_25_qn), .Q(d_ff_23_q[2]), .Qn(d_ff_25_qn), .reset(or_13_out));  // open: preset, en
  D_Flip_Flop d_ff_26 (
    .clk(d_ff_25_qn), .D(d_ff_26_qn), .Q(d_ff_23_q[3]), .Qn(d_ff_26_qn), .reset(or_13_out));  // open: preset, en
  D_Flip_Flop d_ff_27 (
    .clk(d_ff_26_qn), .D(d_ff_27_qn), .Q(d_ff_23_q[4]), .Qn(d_ff_27_qn), .reset(or_13_out));  // open: preset, en
  D_Flip_Flop d_ff_28 (
    .clk(d_ff_27_qn), .D(d_ff_28_qn), .Q(d_ff_23_q[5]), .Qn(d_ff_28_qn), .reset(or_13_out));  // open: preset, en
  or or_13 (or_13_out, RESET, min00);
  Subtractor #(.width(6)) subtractor_2 (.a(d_ff_17_q), .b(d_ff_23_q), .out(M));  // open: bin, bout
  Comparator #(.width(6), .mode("unsigned")) comparator_4 (
    .a({6{1'b0}}), .b(M), .eq(_00_min_t), .lt(_00_min));  // open: gt
  Comparator #(.width(6), .mode("unsigned")) comparator_5 (
    .a(6'b111100), .b(M), .eq(_60_min_t), .lt(_60_min));  // open: gt
  Comparator #(.width(6), .mode("unsigned")) comparator_6 (
    .a(6'b111011), .b(M), .gt(_59_min_t), .eq(_59_min));  // open: lt
  and and_13 (_59_59, _59_min, S_yes, _59_sec);
  and and_14 (_00_00, _00_min_t, S_yes_t, _00_sec);
  and and_15 (M_plus_plus, _59_min_t, S_yes, _60_sec_t);
  and and_16 (M_minus_minus, _00_min, S_yes_t, _60_sec);
  and and_17 (reset1, _59_min, S_yes, _60_sec_t);
  and and_18 (reset2, _60_min_t, M_yes, _59_sec);
  and and_19 (min00, _60_min, M_yes_t);
  and and_20 (reset3, _60_min_t, M_yes);
  and and_21 (p59, _59_min, _59_sec);
  and and_22 (p0, _00_min_t, _00_sec);
  or or_14 (RESET, reset3, reset_input, reset1, reset2);

  assign mode_2 = mode;

  // Other names for the same wires on the sheet: PauseCheck0 = pause_led; PauseCheck1 = pause_led_2;
  //   sec00 = M_plus_plus; sec59 = M_minus_minus

  // Notes on the sheet:
  //   Pause dahil sa mode
endmodule
